// Logisim project scheme.circ as structural Verilog
module Arithmetic_Logic_Unit (
  input  C,
  input  R,
  input  EZ,
  input  i,
  input  EF,
  input  LX,
  input  LY,
  input  [7:0] D,
  input  [7:0] OP,
  output [7:0] S
);

  wire Adc___Sbb_o, and_1_out, and_2_out, and_3_out, and_4_out, and_5_out, and_6_out, and_7_out, or_1_out,
       or_2_out, Right_Shift_o;
  wire [3:0] or_3_out;
  wire [7:0] Adc___Sbb_s, Bitwise_AND_and, Bitwise_NOR_nor, Bitwise_OR_or, Decoder_d, Reg_X_q, Reg_Y_q,
       Right_Shift_sft;

  D_Latch Reg_X (.D(D), .R(R), .E(and_1_out), .Q(Reg_X_q));
  and and_1 (and_1_out, C, LX);
  D_Latch Reg_Y (.D(D), .R(R), .E(and_2_out), .Q(Reg_Y_q));
  and and_2 (and_2_out, LY, C);
  and and_3 (and_3_out, OP[4], OP[6]);
  and and_4 (and_4_out, and_3_out, ~OP[5]);  // AND_Gate
  and and_5 (and_5_out, OP[5], OP[6]);
  // Probe on Reg_X_q
  // Probe on Reg_Y_q
  Decoder Decoder (.C(OP[6:4]), .E(EZ), .D(Decoder_d));
  BitAnd Bitwise_AND (.A(Reg_X_q), .B(Reg_Y_q), .AND(Bitwise_AND_and));
  BitOr Bitwise_OR (.A(Reg_X_q), .B(Reg_Y_q), .OR(Bitwise_OR_or));
  BitNor Bitwise_NOR (.A(Reg_X_q), .B(Reg_Y_q), .NOR(Bitwise_NOR_nor));
  RightShift Right_Shift (.A(Reg_X_q), .i(i), .o(Right_Shift_o), .SFT(Right_Shift_sft));
  AdcSbb Adc___Sbb (.M(Decoder_d[7]), .i(i), .A(Reg_X_q), .B(Reg_Y_q), .S(Adc___Sbb_s), .o(Adc___Sbb_o));
  Comparator Comparator (.A(Reg_X_q), .B(Reg_Y_q), .A_B(or_3_out[1]), .A_B_2(or_3_out[2]), .A_B_3(or_3_out[3]));
  or or_1 (or_1_out, EF, Decoder_d[1]);
  assign S = Decoder_d[2] ? Bitwise_AND_and : 8'bz;  // Controlled_Buffer controlled_buffer_1
  assign S = Decoder_d[3] ? Bitwise_OR_or : 8'bz;  // Controlled_Buffer controlled_buffer_2
  assign S = Decoder_d[4] ? Bitwise_NOR_nor : 8'bz;  // Controlled_Buffer controlled_buffer_3
  assign S = Decoder_d[5] ? Right_Shift_sft : 8'bz;  // Controlled_Buffer controlled_buffer_4
  and and_6 (and_6_out, Right_Shift_o, and_4_out);
  or or_2 (or_2_out, Decoder_d[6], Decoder_d[7]);
  or or_3 (or_3_out[0], and_6_out, and_7_out);
  and and_7 (and_7_out, Adc___Sbb_o, and_5_out);
  assign S = or_2_out ? Adc___Sbb_s : 8'bz;  // Controlled_Buffer controlled_buffer_5
  assign S = or_1_out ? {4'b0000, or_3_out} : 8'bz;  // Controlled_Buffer controlled_buffer_6
endmodule
